# Fritzing sketch main (saved by Fritzing 1.0.1rc)
breadboards: 1

parts:
  A2 = Arduino Nano ESP32
  S2 = Momentary Switch [package=ksa_sealed_tac_switch]
  KY-2 = Keyes Relay [package=THT]
  M2 = DC Motor [voltage_(max)=6V voltage_(min)=3V]
  LED2 = smd LED [color="Yellow (585nm)" package="0603 [SMD]"]
  R4 = Resistor [tolerance=±5% resistance=220 package="0402 [SMD]"]
  R5 = Resistor [tolerance=±5% resistance=220 package="0402 [SMD]"]
  Chirp!_Soil_Moisture_Sensor1 = Chirp! Soil Moisture Sensor v2.7.3
  VCC2 = Battery block 9V
  U3 = Voltage Regulator - 5V [package="DPak [SMD]"]
  LED3 = smd LED [color="Green (555nm)" package="0603 [SMD]"]

nets:
  N1: A2.Pin_4, Chirp!_Soil_Moisture_Sensor1.pin_3
  N2: A2.Pin_12, S2.4, KY-2.power, Chirp!_Soil_Moisture_Sensor1.Pin_1
  N3: A2.Pin_14, A2.Pin_19, KY-2.ground, KY-2.NO, R4.Pin_1, R5.Pin_1, Chirp!_Soil_Moisture_Sensor1.pin_5, VCC2.-, U3.GND
  N4: A2.Pin_22, S2.1
  N5: A2.Pin_24, LED2.anode
  N6: A2.Pin_26, LED3.anode
  N7: A2.Pin_30, KY-2.signal
  N8: KY-2.C, M2.pin_1
  N9: M2.pin_2, U3.output_voltage
  N10: LED2.cathode, R4.Pin_0
  N11: R5.Pin_0, LED3.cathode
  N12: VCC2.+, U3.input_voltage

notes:
  IN / VCC / GND
  VIN / GND / VOUT
  The actual sensor does not communicate via SPI but returns an analogic value. Consider the "SDA/MOSI" pin as this analog output.
  Water pump

custom parts:
  Arduino Nano ESP32: Arduino® Nano ESP32 smd.
  Keyes Relay: The Keyes 5V relay module is suitable for SCM development, home appliance control. It uses a 5V~12V TIL control signal which can control DC / AC signal.
